# Fritzing sketch fan-controller (saved by Fritzing 0.9.9b)
breadboards: 1

parts:
  WeMos_D1_Mini1 = WeMos D1 Mini
  U1 = RELAY-SOLIDSTATE [package=relay-s108t02]
  U2 = RELAY-SOLIDSTATE [package=relay-s108t02]
  Q1 = TRANSISTOR_NPN [package=to-92]
  Q2 = TRANSISTOR_NPN [package=to-92]
  S1 = Pushbutton [package="[THT]"]
  S2 = Pushbutton [package="[THT]"]
  LED1 = LEDs [package=led10mm]
  R1 = Resistor [tolerance=±5% power=0.25 resistance=220 package=THT]

nets:
  N1: WeMos_D1_Mini1.D1, S2.Pin_3, S2.Pin_4
  N2: WeMos_D1_Mini1.D2, S1.Pin_3, S1.Pin_4
  N3: WeMos_D1_Mini1.D5, Q2.B
  N4: WeMos_D1_Mini1.D6, Q1.B
  N5: U1.T1, U2.T1
  N6: U1.+, U2.+, R1.Pin_1
  N7: U1.-, Q1.C
  N8: U2.-, Q2.C
  N9: Q1.E, Q2.E, S1.Pin_1, S1.Pin_2, S2.Pin_1, S2.Pin_2, LED1.C
  N10: LED1.A, R1.Pin_0

notes:
  AC Line in
  AC Out to fan
